# Fritzing sketch lampicka_no_connector (saved by Fritzing 0.9.3b)
circuit board: 2.16851cm x 2.33071cm
breadboards: 1

parts:
  Espessif_Serial_Wifi_Modul_1 = ESP8266 ESP01 [part_number=ESP8266 package=THT]
  C1 = SMD Capacitor [package=1206]
  C2 = SMD Capacitor [package=1206]
  R2 = Resistor [tolerance=±5% resistance=4.7k package="1206 [SMD]"]
  R1 = Resistor [tolerance=±5% resistance=3.3k package="1206 [SMD]"]
  IC2 = Voltage Regulator LM1117 [package=sot223]
  Power_plug2 = Power plug
  J1 = female alternating pin header, 1 pin [form="♀ (female)"]
  J2 = female alternating pin header, 1 pin [form="♀ (female)"]
  J3 = female alternating pin header, 1 pin [form="♀ (female)"]
  J4 = female alternating pin header, 1 pin [form="♀ (female)"]
  Q1 = NPN-Transistor [package="TO92 [THT]"]
  Q2 = NPN-Transistor [package="TO92 [THT]"]
  R3 = Resistor [tolerance=±5% resistance=3.3k package="1206 [SMD]"]
  R4 = Resistor [tolerance=±5% resistance=4.7k package="1206 [SMD]"]
  R5 = Resistor [tolerance=±5% resistance=4.7k package="1206 [SMD]"]
  R6 = Resistor [tolerance=±5% resistance=4.7k package="1206 [SMD]"]
  Q3 = NPN-Transistor [package="TO92 [THT]"]
  R7 = Resistor [tolerance=±5% resistance=3.3k package="1206 [SMD]"]
  Součástka1 = IR Receiver Breakout [package=PCB]
  J6 = female alternating pin header, 1 pin [form="♀ (female)"]
  J7 = female alternating pin header, 1 pin [form="♀ (female)"]
  J5 = rounded female pin header, 1 pin [form="♀ (female rounded)"]
  J5_2 = male pin header, 1 pin [form="♂ (male)"]
  J5_3 = female pin header, 1 pin [form="♀ (female)"]
  J5_4 = female pin header, 1 pin [form="♀ (female)" part_number=3.3V]

nets:
  GND: Espessif_Serial_Wifi_Modul_1.GND, C1.2, C2.2, IC2.ADJ, Power_plug2.GND, Q1.E, Q2.E, Q3.E, Součástka1.GND, J6.pin1
  N1: Espessif_Serial_Wifi_Modul_1.RXD, R6.Pin_1, R7.Pin_0
  N2: Espessif_Serial_Wifi_Modul_1.TXD, R3.Pin_0, R5.Pin_1
  3.3V: Espessif_Serial_Wifi_Modul_1.VCC, Espessif_Serial_Wifi_Modul_1.GPIO16, Espessif_Serial_Wifi_Modul_1.CH_PD, C2.1, R2.Pin_1, R1.Pin_1, IC2.OUT, R3.Pin_1, R7.Pin_1, Součástka1.VCC, J5.pin1, J5_2.pin1, J5_3.pin1, J5_4.pin1
  N3: Espessif_Serial_Wifi_Modul_1.GPIO00, R1.Pin_0, R4.Pin_1
  N4: Espessif_Serial_Wifi_Modul_1.GPIO02, R2.Pin_0, Součástka1.OUT, J7.pin1
  12V: C1.1, IC2.IN, Power_plug2.VCC, J4.pin1
  N5: J1.pin1, Q2.C
  N6: J2.pin1, Q3.C
  N7: J3.pin1, Q1.C
  N8: Q1.B, R4.Pin_0
  N9: Q2.B, R6.Pin_0
  N10: R5.Pin_0, Q3.B

notes:
  3.3V
  GND
  IR

custom parts:
  ESP8266 ESP01: Generic WiFi Module based on the ESP8266 with onboard PCB antenna and UART communications
  SMD Capacitor: Capacitor Standard 0603 ceramic capacitor, and 0.1 leaded capacitor.
  Power plug: power plug
